# Fritzing sketch 7segment_02 (saved by Fritzing 0.9.3b)
breadboards: 1

parts:
  부품1 = Arduino Uno (Rev3)
  DI1 = 7-Segment LED Display [package=THT]
  S1 = Momentary Switch [package=ksa_sealed_tac_switch]
  R1 = Resistor [tolerance=±5% resistance=220 package=THT]
  R2 = Resistor [tolerance=±5% resistance=220 package=THT]
  R3 = Resistor [tolerance=±5% resistance=220 package=THT]
  R4 = Resistor [tolerance=±5% resistance=220 package=THT]
  R5 = Resistor [tolerance=±5% resistance=220 package=THT]
  R6 = Resistor [tolerance=±5% resistance=220 package=THT]
  R7 = Resistor [tolerance=±5% resistance=220 package=THT]
  R8 = Resistor [tolerance=±5% resistance=220 package=THT]

nets:
  N1: 부품1.D8, R3.Pin_0
  N2: 부품1.D13/SCK, S1.1
  N3: 부품1.D2, R5.Pin_1
  N4: 부품1.D3_PWM, R4.Pin_1
  N5: 부품1.D4, R2.Pin_1
  N6: 부품1.D5_PWM, R1.Pin_1
  N7: 부품1.D6_PWM, R6.Pin_0
  N8: 부품1.D7, R7.Pin_0
  N9: 부품1.5V, DI1.commAnode#2
  N10: 부품1.GND, R8.Pin_1
  N11: DI1.cathodeE, R2.Pin_0
  N12: DI1.cathodeD, R1.Pin_0
  N13: DI1.cathodeC, R3.Pin_1
  N14: DI1.cathodeB, R7.Pin_1
  N15: DI1.cathodeA, R6.Pin_1
  N16: DI1.cathodeF, R4.Pin_0
  N17: DI1.cathodeG, R5.Pin_0
  N18: S1.3, R8.Pin_0
