# Fritzing sketch lightsensor_01 (saved by Fritzing 0.9.3b)
breadboards: 1

parts:
  부품1 = Arduino Uno (Rev3)
  R1 = Resistor [tolerance=±5% resistance=220 package=THT]
  R2 = Photocell (LDR) [package=THT]
  LED1 = LED - 5mm [color="Red (633nm)" package="5 mm [THT]"]
  R3 = Resistor [tolerance=±5% resistance=10k package=THT]

nets:
  N1: 부품1.A0, R1.Pin_0
  N2: 부품1.A1, 부품1.5V, R3.Pin_0
  N3: 부품1.GND, R2.pin_1, LED1.cathode
  N4: R1.Pin_1, LED1.anode
  N5: R2.pin_0, R3.Pin_1
