# Fritzing sketch servo_01 (saved by Fritzing 0.9.3b)
breadboards: 1

parts:
  부품1 = Arduino Uno (Rev3)
  J1 = Basic Servo

nets:
  N1: 부품1.D9_PWM, J1.pulse
  5V: 부품1.5V, J1.vcc
  GND: 부품1.GND, J1.gnd

// code stored in the sketch: servo_01.ino
#include <Servo.h> 
 
int servoPin = 9;
Servo servo; 
int angle = 0; // servo position in degrees 
void setup() 
{ 
    servo.attach(servoPin); 
} 
void loop() 
{ 
  // scan from 0 to 180 degrees
  for(angle = 0; angle < 180; angle++) 
  { 
    servo.write(angle); 
    delay(15); 
  } 
  // now scan back from 180 to 0 degrees
  for(angle = 180; angle > 0; angle--) 
  { 
    servo.write(angle); 
    delay(15); 
  } 
}
